# Fritzing sketch caida_libre (saved by Fritzing 0.9.3b)
breadboards: 1

parts:
  Componente1 = Arduino Uno (Rev3) - ICSP
  CNY70-1 = CNY70 [package=cny70-side]
  R1 = Resistor [tolerance=±5% resistance=220 package="2010 [SMD]"]
  R2 = Resistor [tolerance=±5% resistance=10k package="2010 [SMD]"]
  CNY70-2 = CNY70 [package=cny70-side]
  R3 = Resistor [tolerance=±5% resistance=220 package="2010 [SMD]"]
  R4 = Resistor [tolerance=±5% resistance=10k package="2010 [SMD]"]
  Componente2 = LCD1602-I2C
  S1 = Pushbutton [package="[SMD]"]
  R5 = Resistor [tolerance=±5% resistance=10k package="2010 [SMD]"]

nets:
  N1: Componente1.A0, CNY70-1.C, R2.Pin_0
  N2: Componente1.A1, CNY70-2.C, R4.Pin_0
  N3: Componente1.A4/SDA, Componente2.SDA
  N4: Componente1.A5/SCL, Componente2.SCL
  GND: Componente1.GND, R1.Pin_1, R2.Pin_1, R3.Pin_1, R4.Pin_1, Componente2.GND
  N5: Componente1.D7, S1.Pin_1, S1.Pin_2, R5.Pin_0
  5V: Componente1.5V, CNY70-1.A, CNY70-1.E, CNY70-2.A, CNY70-2.E, Componente2.VCC, S1.Pin_3, S1.Pin_4, R5.Pin_1
  N6: CNY70-1.K, R1.Pin_0
  N7: CNY70-2.K, R3.Pin_0

notes:
  Pantalla LCD funcionando con protocolo bus serie I2C. SCL (señal de reloj) y SDA (datos serie)
  CNY70. Emisor-Sensor infrarrojo
  https://www.luisllamas.es/arduino-lcd-i2c/
  https://hetpro-store.com/TUTORIALES/cny70-sensor-optico/
  RESETEO

custom parts:
  CNY70: PHOTOTRANSISTOR
  LCD1602-I2C: A standard character display, usually with 2x16 characters. Comes in many colors with LCM1602 IIC attached.
