# Fritzing sketch Pendulo (saved by Fritzing 0.9.3b)
breadboards: 1

parts:
  Componente1 = Arduino Ethernet Shield (Rev3)
  S3 = Momentary Switch [package=ksa_sealed_tac_switch]
  R1 = Resistor [tolerance=±5% resistance=10k package="2512 [SMD]"]
  R3 = Resistor [tolerance=±5% resistance=4.7k package="2512 [SMD]"]
  R4 = Photocell (LDR) [package=THT]
  LD1 = LD

nets:
  N1: Componente1.D8, LD1.anode
  N2: Componente1.GND, R1.Pin_0, R3.Pin_0, LD1.cathode
  N3: Componente1.A0, R3.Pin_1, R4.pin_0
  N4: Componente1.PWM_D5, S3.3, R1.Pin_1
  N5: Componente1.5V, S3.1, R4.pin_1

custom parts:
  LD: A Generic Red Dot Laser Diode Module (~5mW)
