# Fritzing sketch Sensor de temperatura (saved by Fritzing 0.9.3b)

parts:
  U1 = ESP8266 NodeMCU LoLin base
  DS1 = DS18B20 1-Wire Temperature Sensor [part_number=DS18B20]
  R1 = Resistor [tolerance=±5% resistance=4.7k package="0402 [SMD]"]

nets:
  N1: U1.3V1-0, U1.3V3-0, U1.3V3-2, DS1.VDD, R1.Pin_1
  N2: U1.D3-0, U1.D3-2, U1.D3-3, DS1.DQ, R1.Pin_0
  N3: U1.GND3-3, U1.GND8-0, DS1.GND

custom parts:
  ESP8266 NodeMCU LoLin base: ESP8266 based NodeMCU Base
